// Logisim project Assignment 3 - Bader & Keegan.circ as structural Verilog
module main (
  input  in_1,
  input  in_2
);

  wire _2_4_Decoder_f0, _2_4_Decoder_f1, _2_4_Decoder_f2, _2_4_Decoder_f3, clock_1_out, or_1_out;

  buf or_1 (or_1_out, _2_4_Decoder_f3);  // OR_Gate
  Decoder _2_4_Decoder (
    .I0(in_1), .I1(in_2), .F0(_2_4_Decoder_f0), .F1(_2_4_Decoder_f1), .F2(_2_4_Decoder_f2),
    .F3(_2_4_Decoder_f3));
  // OR_Gate or_2 is placed but not wired
  Clock clock_1 (.out(clock_1_out));
  _2_bit_register MAR (.Clock(clock_1_out));  // open: Enable, D0, D1, out_5, out_6
  _4_bit_register MDR (.Clock(clock_1_out), .Enable(or_1_out));  // open: D0, D1, D2, D3, O0, O1, O2, O3
  _4_bit_register R0 (.Clock(clock_1_out), .Enable(clock_1_out));  // open: D0, D1, D2, D3, O0, O1, O2, O3
  _4_bit_register R1 (
    .Clock(clock_1_out), .Enable(_2_4_Decoder_f1), .D0(_2_4_Decoder_f2));  // open: D1, D2, D3, O0, O1, O2, O3
  _4_bit_register R2 (.Clock(clock_1_out), .Enable(_2_4_Decoder_f0));  // open: D0, D1, D2, D3, O0, O1, O2, O3
  ALU ALU ();  // open: x, in_2, y, in_4, in_5, in_6, in_7, in_8, carry_in, F1, F2, out_12, out_13, out_14, out_15, carry_out

  // Notes on the sheet:
  //   Circuit by Bader Abdulwaseem and Keegan Barnett
endmodule

module Logic_unit (
  input  A,
  input  B,
  output A_AND_B,
  output A_OR_B,
  output NOT_A,
  output NOT_B
);

  and and_1 (A_AND_B, A, B);
  or or_1 (A_OR_B, A, B);
  not not_1 (NOT_A, A);
  not not_2 (NOT_B, B);
endmodule

module Decoder (
  input  I0,
  input  I1,
  output F0,
  output F1,
  output F2,
  output F3
);

  wire not_1_out, not_2_out;

  not not_1 (not_1_out, I0);
  not not_2 (not_2_out, I1);
  and and_1 (F0, not_1_out, not_2_out);
  and and_2 (F1, I0, not_2_out);
  and and_3 (F2, not_1_out, I1);
  and and_4 (F3, I0, I1);

  // Notes on the sheet:
  //   I0: pull=down
  //   I1: pull=down
endmodule

module multiplexer (
  input  I1,
  input  I0,
  input  L0,
  input  L1,
  input  L2,
  input  L3,
  output out_7
);

  wire and_1_out, and_2_out, and_3_out, and_4_out, decoder_1_f0, decoder_1_f1, decoder_1_f2, decoder_1_f3;

  Decoder decoder_1 (.I0(I0), .I1(I1), .F0(decoder_1_f0), .F1(decoder_1_f1), .F2(decoder_1_f2), .F3(decoder_1_f3));
  and and_1 (and_1_out, decoder_1_f0, L0);
  and and_2 (and_2_out, decoder_1_f1, L1);
  and and_3 (and_3_out, decoder_1_f2, L2);
  and and_4 (and_4_out, decoder_1_f3, L3);
  or or_1 (out_7, and_1_out, and_2_out, and_3_out, and_4_out);

  // Notes on the sheet:
  //   L0: pull=down
  //   L2: pull=down
  //   L3: pull=down
  //   L1: pull=down
  //   I1: pull=down
  //   I0: pull=down
endmodule

module _4_bit_register (
  input  Clock,
  input  Enable,
  input  D0,
  input  D1,
  input  D2,
  input  D3,
  output O0,
  output O1,
  output O2,
  output O3
);

  wire and_1_out;

  and and_1 (and_1_out, Clock, Enable);
  D_Flip_Flop d_ff_1 (.clk(and_1_out), .D(D0), .Q(O0));  // open: Qn, preset, en, reset
  D_Flip_Flop d_ff_2 (.clk(and_1_out), .D(D1), .Q(O1));  // open: Qn, preset, en, reset
  D_Flip_Flop d_ff_3 (.clk(and_1_out), .D(D2), .Q(O2));  // open: Qn, preset, en, reset
  D_Flip_Flop d_ff_4 (.clk(and_1_out), .D(D3), .Q(O3));  // open: Qn, preset, en, reset
endmodule

module _2_bit_register (
  input  Clock,
  input  Enable,
  input  D0,
  input  D1,
  output out_5,
  output out_6
);

  wire and_1_out;

  and and_1 (and_1_out, Clock, Enable);
  D_Flip_Flop d_ff_1 (.clk(and_1_out), .D(D0), .Q(out_5));  // open: Qn, preset, en, reset
  D_Flip_Flop d_ff_2 (.clk(and_1_out), .D(D1), .Q(out_6));  // open: Qn, preset, en, reset
endmodule

module ALU (
  input  x,
  input  in_2,
  input  y,
  input  in_4,
  input  in_5,
  input  in_6,
  input  in_7,
  input  in_8,
  input  carry_in,
  input  F1,
  input  F2,
  output out_12,
  output out_13,
  output out_14,
  output out_15,
  output carry_out
);

  wire bit_slice_1_carry_out, bit_slice_2_carry_out, bit_slice_3_carry_out;

  Bit_Slice bit_slice_1 (
    .x(x), .y(in_5), .ci(carry_in), .f0(F2), .f1(F1), .Output(out_12), .Carry_out(bit_slice_1_carry_out));
  Bit_Slice bit_slice_2 (
    .x(in_2), .y(in_6), .ci(bit_slice_1_carry_out), .f0(F2), .f1(F1), .Output(out_13),
    .Carry_out(bit_slice_2_carry_out));
  Bit_Slice bit_slice_3 (
    .x(y), .y(in_7), .ci(bit_slice_2_carry_out), .f0(F2), .f1(F1), .Output(out_14),
    .Carry_out(bit_slice_3_carry_out));
  Bit_Slice bit_slice_4 (
    .x(in_4), .y(in_8), .ci(bit_slice_3_carry_out), .f0(F2), .f1(F1), .Output(out_15), .Carry_out(carry_out));
endmodule

module Bit_Slice (
  input  x,
  input  y,
  input  ci,
  input  f0,
  input  f1,
  output Output,
  output Carry_out
);

  wire A_AND_B_out, A_OR_B_out, Decoder_p3, Decoder_p4, Decoder_p5, Decoder_p6, Full_Adder_p4,
       Logic_Unit_a_and_b, Logic_Unit_a_or_b, Logic_Unit_not_a, Logic_Unit_not_b, NOT_A_out, NOT_B_out;

  Logic_unit Logic_Unit (
    .A(x), .B(y), .A_AND_B(Logic_Unit_a_and_b), .A_OR_B(Logic_Unit_a_or_b), .NOT_A(Logic_Unit_not_a),
    .NOT_B(Logic_Unit_not_b));
  // Full_Adder Full_Adder: pin names not known; wires that end beside it: x, y, ci, Full_Adder_p4
  // _2_4_Decoder Decoder: pin names not known; wires that end beside it: f0, f1, Decoder_p3, Decoder_p4, Decoder_p5, Decoder_p6, Decoder_p5
  and A_AND_B (A_AND_B_out, Logic_Unit_a_and_b, Decoder_p3);
  and A_OR_B (A_OR_B_out, Logic_Unit_a_or_b, Decoder_p4);
  buf NOT_A (NOT_A_out, Logic_Unit_not_a);  // AND_Gate
  and NOT_B (NOT_B_out, Logic_Unit_not_b, Decoder_p6);
  and Carry (Carry_out, Full_Adder_p4, Decoder_p6);
  or or_1 (Output, A_AND_B_out, A_OR_B_out, NOT_A_out, NOT_B_out);
endmodule

module Full_Adder (
  input  x,
  input  y,
  input  z,
  output Sum,
  output Carry_Out
);

  wire and_1_out, and_2_out, xor_1_out;

  xor xor_1 (xor_1_out, y, z);
  and and_1 (and_1_out, y, z);
  xor xor_2 (Sum, x, xor_1_out);
  and and_2 (and_2_out, x, xor_1_out);
  or or_1 (Carry_Out, and_2_out, and_1_out);
endmodule
