// Logisim project Assignment 3 - Sharjeel.circ as structural Verilog
module main (
  input  [1:0] Address,
  input  R_W,
  input  [1:0] S_A,
  input  [1:0] S_B,
  input  ENA,
  input  [1:0] Selector,
  input  [2:0] Function,
  input  ENB
);

  wire Clock_2_out, Clock_out, n2_4_decoder_1_f0, n2_4_decoder_1_f1, n2_4_decoder_1_f2, n2_4_decoder_1_f3,
       or_2_out;
  wire [1:0] MAR_output;
  wire [3:0] alu_1_output, MDR_output, n4_bit_multiplexer_1_output, n4_bit_multiplexer_2_output, or_1_out,
       R0_output, R1_output, R2_output, ram_1_data;

  Clock Clock (.out(Clock_out));
  _2_4_Decoder u_2_4_decoder_1 (
    .Input(Selector), .F0(n2_4_decoder_1_f0), .F1(n2_4_decoder_1_f1), .F2(n2_4_decoder_1_f2),
    .F3(n2_4_decoder_1_f3));
  assign or_1_out = alu_1_output | ram_1_data;  // OR_Gate or_1, 4 bits wide
  or or_2 (or_2_out, n2_4_decoder_1_f3, R_W);
  _2_bit_Register MAR (.Input(Address), .Output(MAR_output), .Clock(Clock_out));  // open: Enable
  _4_bit_Register MDR (.Input(or_1_out), .Output(MDR_output), .Enable(or_2_out), .Clock(Clock_out));
  _4_bit_Register R0 (.Input(alu_1_output), .Output(R0_output), .Enable(n2_4_decoder_1_f2), .Clock(Clock_out));
  _4_bit_Register R1 (.Input(alu_1_output), .Output(R1_output), .Enable(n2_4_decoder_1_f1), .Clock(Clock_out));
  _4_bit_Register R2 (.Input(alu_1_output), .Output(R2_output), .Enable(n2_4_decoder_1_f0), .Clock(Clock_out));
  _4_bit_Multiplexer u_4_bit_multiplexer_1 (
    .Select(S_A), .Input_0(R2_output), .Input_1(R1_output), .Input_2(R0_output), .Input_3(MDR_output),
    .Output(n4_bit_multiplexer_1_output));
  _4_bit_Multiplexer u_4_bit_multiplexer_2 (
    .Select(S_B), .Input_0(R2_output), .Input_1(R1_output), .Input_2(R0_output), .Input_3(MDR_output),
    .Output(n4_bit_multiplexer_2_output));
  ALU alu_1 (
    .A(n4_bit_multiplexer_1_output), .B(n4_bit_multiplexer_2_output), .Function(Function), .ENA(ENA),
    .ENB(ENB), .Output(alu_1_output));  // open: Carry_out, Carry_in
  Clock Clock_2 (.out(Clock_2_out));
  RAM #(.addrWidth(2), .dataWidth(4)) ram_1 (
    .addr(MAR_output), .data(ram_1_data), .clk(Clock_2_out), .ld(R_W));  // open: sel, clr
endmodule

module HA (
  input  x,
  input  y,
  output Sum,
  output Carry
);

  xor xor_1 (Sum, x, y);
  and and_1 (Carry, x, y);
endmodule

module FA (
  input  x,
  input  y,
  input  z,
  output Sum,
  output Carry_Out
);

  wire and_1_out, and_2_out, xor_1_out;

  xor xor_1 (xor_1_out, y, z);
  and and_1 (and_1_out, y, z);
  xor xor_2 (Sum, x, xor_1_out);
  and and_2 (and_2_out, x, xor_1_out);
  or or_1 (Carry_Out, and_2_out, and_1_out);
endmodule

// Decd
module _2_4_Decoder (
  input  [1:0] Input,
  output F0,
  output F1,
  output F2,
  output F3
);

  wire not_1_out, not_2_out;

  not not_1 (not_1_out, Input[0]);
  not not_2 (not_2_out, Input[1]);
  and and_1 (F0, not_1_out, not_2_out);
  and and_2 (F1, not_1_out, Input[1]);
  and and_3 (F2, Input[0], not_2_out);
  and and_4 (F3, Input[0], Input[1]);
endmodule

module _3_8_Decoder (
  input  [2:0] Input,
  output F0,
  output F1,
  output F2,
  output F3,
  output F4,
  output F5,
  output F6,
  output F7
);

  wire not_1_out, not_2_out, not_3_out;

  not not_1 (not_1_out, Input[0]);
  not not_2 (not_2_out, Input[1]);
  not not_3 (not_3_out, Input[2]);
  and and_1 (F0, not_3_out, not_2_out, not_1_out);
  and and_2 (F1, not_3_out, not_2_out, Input[0]);
  and and_3 (F2, not_3_out, Input[1], not_1_out);
  and and_4 (F3, not_3_out, Input[1], Input[0]);
  and and_5 (F4, Input[2], not_2_out, not_1_out);
  and and_6 (F5, Input[2], not_2_out, Input[0]);
  and and_7 (F6, Input[2], Input[1], not_1_out);
  and and_8 (F7, Input[2], Input[1], Input[0]);
endmodule

module Logic_Unit (
  input  x,
  input  y,
  output xy,
  output x_y,
  output y_prime,
  output x_prime
);

  and and_1 (xy, x, y);
  or or_1 (x_y, x, y);
  not not_1 (y_prime, y);
  not not_2 (x_prime, x);
endmodule

module Bit_Slice (
  input  x,
  input  y,
  input  Carry_In,
  input  [2:0] Function,
  output Output,
  output Carry_out
);

  wire A___B_out, A_AND_B_out, A_OR_B_out, Decoder_f0, Decoder_f1, Decoder_f2, Decoder_f3, Decoder_f4,
       Full_Adder_carry_out, Full_Adder_sum, Logic_Unit_x_prime, Logic_Unit_x_y, Logic_Unit_xy,
       Logic_Unit_y_prime, Not_A_out, Not_B_out;

  Logic_Unit Logic_Unit (
    .x(x), .y(y), .xy(Logic_Unit_xy), .x_y(Logic_Unit_x_y), .y_prime(Logic_Unit_y_prime),
    .x_prime(Logic_Unit_x_prime));
  FA Full_Adder (.x(x), .y(y), .z(Carry_In), .Sum(Full_Adder_sum), .Carry_Out(Full_Adder_carry_out));
  _3_8_Decoder Decoder (
    .Input(Function), .F0(Decoder_f0), .F1(Decoder_f1), .F2(Decoder_f2), .F3(Decoder_f3), .F4(Decoder_f4));  // open: F5, F6, F7
  and A_AND_B (A_AND_B_out, Logic_Unit_xy, Decoder_f0);
  and A_OR_B (A_OR_B_out, Logic_Unit_x_y, Decoder_f1);
  and Not_A (Not_A_out, Logic_Unit_y_prime, Decoder_f2);
  and Not_B (Not_B_out, Logic_Unit_x_prime, Decoder_f3);
  and A___B (A___B_out, Full_Adder_sum, Decoder_f4);
  and and_1 (Carry_out, Full_Adder_carry_out, Decoder_f4);
  or or_1 (Output, A_AND_B_out, A_OR_B_out, Not_B_out, Not_A_out, A___B_out);
endmodule

module ALU (
  input  [3:0] A,
  input  [3:0] B,
  input  ENA,
  input  ENB,
  input  Carry_in,
  input  [2:0] Function,
  output Carry_out,
  output [3:0] Output
);

  wire and_1_out, and_2_out, and_3_out, and_4_out, and_5_out, and_6_out, and_7_out, and_8_out,
       Bit_Slice_2_carry_out, Bit_Slice_3_carry_out, Bit_Slice_carry_out;

  and and_1 (and_1_out, A[0], ENA);
  and and_2 (and_2_out, A[1], ENA);
  and and_3 (and_3_out, A[2], ENA);
  and and_4 (and_4_out, A[3], ENA);
  and and_5 (and_5_out, B[0], ENB);
  and and_6 (and_6_out, B[1], ENB);
  and and_7 (and_7_out, B[2], ENB);
  and and_8 (and_8_out, B[3], ENB);
  Bit_Slice Bit_Slice (
    .x(and_1_out), .y(and_5_out), .Carry_In(Carry_in), .Function(Function), .Output(Output[0]),
    .Carry_out(Bit_Slice_carry_out));
  Bit_Slice Bit_Slice_2 (
    .x(and_2_out), .y(and_6_out), .Carry_In(Bit_Slice_carry_out), .Function(Function), .Output(Output[1]),
    .Carry_out(Bit_Slice_2_carry_out));
  Bit_Slice Bit_Slice_3 (
    .x(and_3_out), .y(and_7_out), .Carry_In(Bit_Slice_2_carry_out), .Function(Function), .Output(Output[2]),
    .Carry_out(Bit_Slice_3_carry_out));
  Bit_Slice Bit_Slice_4 (
    .x(and_4_out), .y(and_8_out), .Carry_In(Bit_Slice_3_carry_out), .Function(Function), .Output(Output[3]),
    .Carry_out(Carry_out));
endmodule

// Multiplxr
module _4_bit_Multiplexer (
  input  [1:0] Select,
  input  [3:0] Input_0,
  input  [3:0] Input_1,
  input  [3:0] Input_2,
  input  [3:0] Input_3,
  output [3:0] Output
);

  wire n2_4_decoder_1_f0, n2_4_decoder_1_f1, n2_4_decoder_1_f2, n2_4_decoder_1_f3;
  wire [3:0] n4_bit_activator_1_output, n4_bit_activator_2_output, n4_bit_activator_3_output,
       n4_bit_activator_4_output;

  _2_4_Decoder u_2_4_decoder_1 (
    .Input(Select), .F0(n2_4_decoder_1_f0), .F1(n2_4_decoder_1_f1), .F2(n2_4_decoder_1_f2),
    .F3(n2_4_decoder_1_f3));
  _4_bit_Activator u_4_bit_activator_1 (
    .Input(Input_0), .Enable(n2_4_decoder_1_f0), .Output(n4_bit_activator_1_output));
  _4_bit_Activator u_4_bit_activator_2 (
    .Input(Input_1), .Enable(n2_4_decoder_1_f1), .Output(n4_bit_activator_2_output));
  _4_bit_Activator u_4_bit_activator_3 (
    .Input(Input_2), .Enable(n2_4_decoder_1_f2), .Output(n4_bit_activator_3_output));
  _4_bit_Activator u_4_bit_activator_4 (
    .Input(Input_3), .Enable(n2_4_decoder_1_f3), .Output(n4_bit_activator_4_output));
  assign Output = n4_bit_activator_1_output | n4_bit_activator_2_output | n4_bit_activator_3_output | n4_bit_activator_4_output;  // OR_Gate or_1, 4 bits wide
endmodule

module _4_bit_Comparator (
  input  [3:0] x,
  input  [3:0] y,
  output Output
);

  wire xor_1_out, xor_2_out, xor_3_out, xor_4_out;

  xor xor_1 (xor_1_out, y[0], x[0]);
  xor xor_2 (xor_2_out, y[1], x[1]);
  xor xor_3 (xor_3_out, y[2], x[2]);
  xor xor_4 (xor_4_out, y[3], x[3]);
  nor nor_1 (Output, xor_1_out, xor_2_out, xor_3_out, xor_4_out);
endmodule

module _4_bit_Adder (
  input  [3:0] x,
  input  [3:0] y,
  output Carry_Out,
  output [3:0] Output
);

  wire fa_1_carry_out, fa_2_carry_out, ha_1_carry;

  HA ha_1 (.x(x[0]), .y(y[0]), .Sum(Output[0]), .Carry(ha_1_carry));
  FA fa_1 (.x(x[1]), .y(y[1]), .z(ha_1_carry), .Sum(Output[1]), .Carry_Out(fa_1_carry_out));
  FA fa_2 (.x(x[2]), .y(y[2]), .z(fa_1_carry_out), .Sum(Output[2]), .Carry_Out(fa_2_carry_out));
  FA fa_3 (.x(x[3]), .y(y[3]), .z(fa_2_carry_out), .Sum(Output[3]), .Carry_Out(Carry_Out));
endmodule

// reg\n(4b)
module _4_bit_Register (
  input  [3:0] Input,
  input  Clock,
  input  Enable,
  output [3:0] Output
);

  D_Flip_Flop d_ff_1 (.clk(Clock), .D(Input[0]), .Q(Output[0]), .en(Enable));  // open: Qn, preset, reset
  D_Flip_Flop d_ff_2 (.clk(Clock), .D(Input[1]), .Q(Output[1]), .en(Enable));  // open: Qn, preset, reset
  D_Flip_Flop d_ff_3 (.clk(Clock), .D(Input[2]), .Q(Output[2]), .en(Enable));  // open: Qn, preset, reset
  D_Flip_Flop d_ff_4 (.clk(Clock), .D(Input[3]), .Q(Output[3]), .en(Enable));  // open: Qn, preset, reset
endmodule

// reg\n(2b)
module _2_bit_Register (
  input  [1:0] Input,
  input  Clock,
  input  Enable,
  output [1:0] Output
);

  D_Flip_Flop d_ff_1 (.clk(Clock), .D(Input[0]), .Q(Output[0]), .en(Enable));  // open: Qn, preset, reset
  D_Flip_Flop d_ff_2 (.clk(Clock), .D(Input[1]), .Q(Output[1]), .en(Enable));  // open: Qn, preset, reset
endmodule

// Actv
module _4_bit_Activator (
  input  Enable,
  input  [3:0] Input,
  output [3:0] Output
);

  and and_1 (Output[0], Input[0], Enable);
  and and_2 (Output[1], Input[1], Enable);
  and and_3 (Output[2], Input[2], Enable);
  and and_4 (Output[3], Input[3], Enable);

  // Notes on the sheet:
  //   Enable: pull=down
endmodule
