// Logisim project Assignment 3.circ as structural Verilog: 6 circuits, main circuit main
module main (
);

  Clock clock_1 ();  // open: out
endmodule

module _2_bit_Decoder (
  input  I0,
  input  I1,
  output F0,
  output F1,
  output F2,
  output F3
);

  wire not_1_out, not_2_out;

  not not_1 (not_1_out, I0);
  not not_2 (not_2_out, I1);
  and and_1 (F0, not_1_out, not_2_out);
  and and_2 (F1, not_1_out, I1);
  and and_3 (F2, I0, not_2_out);
  and and_4 (F3, I0, I1);
endmodule

module _4_bit_Multiplexer (
  input  in_1,
  input  in_2,
  input  in_3,
  input  in_4,
  input  in_5,
  input  in_6,
  output out_7
);

  wire and_1_out, and_2_out, and_3_out, and_4_out, not_1_out, not_2_out;

  not not_1 (not_1_out, in_1);
  not not_2 (not_2_out, in_2);
  and and_1 (and_1_out, in_3, not_1_out, not_2_out);
  and and_2 (and_2_out, in_4, not_1_out, in_2);
  and and_3 (and_3_out, in_5, not_2_out, in_1);
  and and_4 (and_4_out, in_6, in_1, in_2);
  or or_1 (out_7, and_1_out, and_2_out, and_3_out, and_4_out);
endmodule

module Rising_Edge (
  input  I0,
  output re
);

  wire not_1_out, not_2_out, not_3_out;

  not not_1 (not_1_out, I0);
  not not_2 (not_2_out, not_1_out);
  not not_3 (not_3_out, not_2_out);
  and and_1 (re, I0, not_3_out);
endmodule

module D_Latch (
  input  D,
  input  E,
  output Q,
  output Q_prime
);

  wire and_1_out, and_2_out, clock_1_out, not_1_out;

  Clock clock_1 (.out(clock_1_out));
  not not_1 (not_1_out, D);
  and and_1 (and_1_out, not_1_out, E, clock_1_out);
  and and_2 (and_2_out, clock_1_out, E, D);
  nor nor_1 (Q, and_1_out, Q_prime);
  nor nor_2 (Q_prime, Q, and_2_out);
endmodule

module _1_bit_Register (
  input  I0,
  output out_2
);

  wire clk_out, rising_edge_1_re;

  Clock clk (.out(clk_out));
  Rising_Edge rising_edge_1 (.I0(clk_out), .re(rising_edge_1_re));
  D_Latch d_latch_1 (.D(I0), .E(rising_edge_1_re), .Q(out_2));  // open: Q_prime
endmodule
