// Logisim project Assignment3.circ as structural Verilog
module main (
  input  in_1,
  input  in_2,
  input  in_3,
  output out_4
);

  wire _2_4_Decoder_f0, _2_4_Decoder_f1, _2_4_Decoder_f2, _2_4_Decoder_f3, clock_1_out, or_1_out;

  buf or_1 (or_1_out, _2_4_Decoder_f3);  // OR_Gate
  Decoder _2_4_Decoder (
    .I0(in_2), .I1(in_3), .F0(_2_4_Decoder_f0), .F1(_2_4_Decoder_f1), .F2(_2_4_Decoder_f2),
    .F3(_2_4_Decoder_f3));
  Clock clock_1 (.out(clock_1_out));
  _2_bit_register MAR (.Clock(clock_1_out));  // open: Enable, D0, D1, out_5, out_6
  _4_bit_register MDR (.Clock(clock_1_out), .Enable(or_1_out));  // open: D0, D1, D2, D3, O0, O1, O2, O3
  _4_bit_register R0 (
    .Clock(clock_1_out), .Enable(clock_1_out), .D0(in_1), .O0(out_4));  // open: D1, D2, D3, O1, O2, O3
  _4_bit_register R1 (
    .Clock(clock_1_out), .Enable(_2_4_Decoder_f1), .D0(_2_4_Decoder_f2));  // open: D1, D2, D3, O0, O1, O2, O3
  _4_bit_register R2 (.Clock(clock_1_out), .Enable(_2_4_Decoder_f0));  // open: D0, D1, D2, D3, O0, O1, O2, O3
endmodule

module Logic_unit (
  input  A,
  input  B,
  output A_AND_B,
  output A_OR_B,
  output NOT_A,
  output NOT_B
);

  and and_1 (A_AND_B, A, B);
  or or_1 (A_OR_B, A, B);
  not not_1 (NOT_A, A);
  not not_2 (NOT_B, B);
endmodule

module Decoder (
  input  I0,
  input  I1,
  output F0,
  output F1,
  output F2,
  output F3
);

  wire not_1_out, not_2_out;

  not not_1 (not_1_out, I0);
  not not_2 (not_2_out, I1);
  and and_1 (F0, not_1_out, not_2_out);
  and and_2 (F1, I0, not_2_out);
  and and_3 (F2, not_1_out, I1);
  and and_4 (F3, I0, I1);

  // Notes on the sheet:
  //   I0: pull=down
  //   I1: pull=down
endmodule

module multiplexer (
  input  I1,
  input  I0,
  input  L0,
  input  L1,
  input  L2,
  input  L3,
  output out_7
);

  wire and_1_out, and_2_out, and_3_out, and_4_out, decoder_1_f0, decoder_1_f1, decoder_1_f2, decoder_1_f3;

  Decoder decoder_1 (.I0(I0), .I1(I1), .F0(decoder_1_f0), .F1(decoder_1_f1), .F2(decoder_1_f2), .F3(decoder_1_f3));
  and and_1 (and_1_out, decoder_1_f0, L0);
  and and_2 (and_2_out, decoder_1_f1, L1);
  and and_3 (and_3_out, decoder_1_f2, L2);
  and and_4 (and_4_out, decoder_1_f3, L3);
  or or_1 (out_7, and_1_out, and_2_out, and_3_out, and_4_out);

  // Notes on the sheet:
  //   L0: pull=down
  //   L2: pull=down
  //   L3: pull=down
  //   L1: pull=down
  //   I1: pull=down
  //   I0: pull=down
endmodule

module _4_bit_register (
  input  Clock,
  input  Enable,
  input  D0,
  input  D1,
  input  D2,
  input  D3,
  output O0,
  output O1,
  output O2,
  output O3
);

  wire and_1_out;

  and and_1 (and_1_out, Clock, Enable);
  D_Flip_Flop d_ff_1 (.clk(and_1_out), .D(D0), .Q(O0));  // open: Qn, preset, en, reset
  D_Flip_Flop d_ff_2 (.clk(and_1_out), .D(D1), .Q(O1));  // open: Qn, preset, en, reset
  D_Flip_Flop d_ff_3 (.clk(and_1_out), .D(D2), .Q(O2));  // open: Qn, preset, en, reset
  D_Flip_Flop d_ff_4 (.clk(and_1_out), .D(D3), .Q(O3));  // open: Qn, preset, en, reset
endmodule

module _2_bit_register (
  input  Clock,
  input  Enable,
  input  D0,
  input  D1,
  output out_5,
  output out_6
);

  wire and_1_out;

  and and_1 (and_1_out, Clock, Enable);
  D_Flip_Flop d_ff_1 (.clk(and_1_out), .D(D0), .Q(out_5));  // open: Qn, preset, en, reset
  D_Flip_Flop d_ff_2 (.clk(and_1_out), .D(D1), .Q(out_6));  // open: Qn, preset, en, reset
endmodule
